# Fritzing sketch water-meter-reader (saved by Fritzing 0.9.4)

parts:
  U1 = TCRT5000 [part_number=TCRT5000 package=THT]
  R1 = Resistor [tolerance=±5% resistance=15k package=THT]
  WeMos_D1_Mini1 = WeMos D1 Mini
  R2 = Resistor [tolerance=±5% resistance=1k package=THT]
  R3 = Resistor [tolerance=±5% resistance=120k package=THT]

nets:
  N1: U1.Pin_1, R1.Pin_0, R3.Pin_0
  GND: U1.Pin_2, U1.Pin_3, WeMos_D1_Mini1.G
  N2: U1.Pin_4, R2.Pin_0
  5V: R1.Pin_1, WeMos_D1_Mini1.5V, R2.Pin_1
  N3: WeMos_D1_Mini1.A0, R3.Pin_1

custom parts:
  TCRT5000: TCRT5000 optical reflective sensor
